# Fritzing sketch CatRepellent_Schema (saved by Fritzing 0.9.3b)
perfboards: 1

parts:
  NRF24L01+ = NRF24L01+ Breakout Board
  C1 = Electrolytic Capacitor [capacitance=4.7µF package="100 mil [THT, electrolytic]"]
  Arduino_Pro_Mini_5V = Arduino Pro Mini (5V)
  Q1 = Basic FET N-Channel [part_number=IRLZ44N package="D2Pak [SMD]"]
  J1 = Screw terminal - 2 pins [part_number="WATER PUMP" package=THT]
  R2 = Resistor [tolerance=±5% resistance=330 package=THT]
  R3 = Resistor [tolerance=±5% resistance=330 package=THT]
  R4 = Resistor [tolerance=±5% resistance=330 package=THT]
  R5 = Resistor [tolerance=±5% resistance=100k package=THT]
  J6 = Screw terminal - 2 pins [part_number="12V Battery" package=THT]
  LED1 = LED - 5mm [color="Red (633nm)" package="5 mm [THT]"]
  LED2 = LED - 5mm [color="Green (565nm)" package="5 mm [THT]"]
  J8 = male pin header, 3 pins [form="♂ (male)" part_number=PIR]
  J7 = male pin header, 2 pins [form="♂ (male)" part_number="Water tank sensor"]
  U1 = mystery part, 4 pins [chip_label=D24V5F5 part_number="POLOLU-2843 D24V5F5 5V"]
  U2 = mystery part, 3 pins [chip_label=LE33 part_number="REGULATOR 3.3V"]

nets:
  GND: NRF24L01+.GND, C1.-, Arduino_Pro_Mini_5V.GND, Q1.source, R5.Pin_1, J6.pin2, LED1.cathode, LED2.cathode, J8.pin3, J7.pin2, U1.pin3, U2.pin2
  3.3V: NRF24L01+.VCC, C1.+, U2.pin1
  CE: NRF24L01+.CE, Arduino_Pro_Mini_5V.D9
  CSN: NRF24L01+.CS, Arduino_Pro_Mini_5V.D10
  SCK: NRF24L01+.SCK, Arduino_Pro_Mini_5V.SCK
  MOSI: NRF24L01+.MOSI, Arduino_Pro_Mini_5V.MOSI
  MISO: NRF24L01+.MISO, Arduino_Pro_Mini_5V.MISO
  IRQ: NRF24L01+.IRQ, Arduino_Pro_Mini_5V.D2
  5V: Arduino_Pro_Mini_5V.VCC, J8.pin1, U1.pin2, U2.pin3
  RED_LED: Arduino_Pro_Mini_5V.A3, R3.Pin_1
  GREEN_LED: Arduino_Pro_Mini_5V.A1, R2.Pin_1
  WATER_SENSOR: Arduino_Pro_Mini_5V.A0, J7.pin1
  PUMP: Arduino_Pro_Mini_5V.D5, R4.Pin_0
  PIR: Arduino_Pro_Mini_5V.D3, J8.pin2
  N1: Q1.Gate, R4.Pin_1, R5.Pin_0
  N2: Q1.drain, J1.pin2
  12V: J1.pin1, J6.pin1, U1.pin1
  N3: R2.Pin_0, LED2.anode
  N4: R3.Pin_0, LED1.anode
