# Fritzing sketch HotTeaAlert_Schema (saved by Fritzing 0.9.3b)
breadboards: 1

parts:
  Arduino1 = Arduino Pro Mini (3.3V)
  U1 = MLX90614 [package=to-39]
  R1 = Resistor [tolerance=±5% resistance=330 package=THT]
  LED1 = RGB LED (com. cathode, rgb) [package="5 mm [THT]"]
  R2 = Resistor [tolerance=±5% resistance=330 package=THT]
  LED2 = RGB LED (com. cathode, rgb) [package="5 mm [THT]"]
  R3 = Resistor [tolerance=±5% resistance=330 package=THT]
  LED3 = RGB LED (com. cathode, rgb) [package="5 mm [THT]"]
  R4 = Resistor [tolerance=±5% resistance=330 package=THT]
  LED4 = RGB LED (com. cathode, rgb) [package="5 mm [THT]"]
  S2 = SWITCH-MOMENTARY-2 [package=tactile-pth]
  NRF24L01+ = NRF24L01+ Breakout Board
  C1 = Electrolytic Capacitor [capacitance=4.7µF package="100 mil [THT, electrolytic]"]

nets:
  GND: Arduino1.GND, U1.VSS, R1.Pin_1, R2.Pin_1, R3.Pin_1, R4.Pin_1, S2.2, NRF24L01+.GND, C1.-
  N1: Arduino1.A4, U1.PWM_SDA
  N2: Arduino1.A5, U1.SCL_VZ
  N3: Arduino1.RESET, S2.1
  3.3V: Arduino1.VCC, NRF24L01+.VCC, C1.+
  POWER_TEMP: Arduino1.A0, U1.VDD
  SCK: Arduino1.SCK, NRF24L01+.SCK
  MISO: Arduino1.MISO, NRF24L01+.MISO
  MOSI: Arduino1.MOSI, NRF24L01+.MOSI
  CSN: Arduino1.D10, NRF24L01+.CS
  CE: Arduino1.D9, NRF24L01+.CE
  BLUE_LED: Arduino1.D5, LED1.blue_anode, LED2.blue_anode, LED3.blue_anode, LED4.blue_anode
  GREEN_LED: Arduino1.D4, LED1.green_anode, LED2.green_anode, LED3.green_anode, LED4.green_anode
  RED_LED: Arduino1.D3, LED1.red_anode, LED2.red_anode, LED3.red_anode, LED4.red_anode
  N4: R1.Pin_0, LED1.common_cathode
  N5: R2.Pin_0, LED2.common_cathode
  N6: R3.Pin_0, LED3.common_cathode
  N7: R4.Pin_0, LED4.common_cathode

notes:
  Hot Tea Alert, V1.0
