# Fritzing sketch Siren_Schema (saved by Fritzing 0.9.3b)
breadboards: 1

parts:
  NRF24L01+ = NRF24L01+ Breakout Board
  C1 = Electrolytic Capacitor [capacitance=4.7µF package="100 mil [THT, electrolytic]"]
  Arduino1 = Arduino Pro Mini (5V)
  Q1 = Basic FET N-Channel [part_number=IRLZ44N package="D2Pak [SMD]"]
  Power_plug1 = Power plug
  J1 = Screw terminal - 2 pins [part_number=SIREN package=THT]
  U1 = Header 8 [part_number=Keypad package=1x08_smd]
  J2 = Piezo Speaker [part_number=Piezo]
  Power_plug2 = Power plug
  R1 = Resistor [tolerance=±5% resistance=220 package=THT]
  LED1 = RGB LED (com. cathode, rgb) [package="5 mm [THT]"]
  R2 = Resistor [tolerance=±5% resistance=220 package=THT]
  R3 = Resistor [tolerance=±5% resistance=220 package=THT]
  R4 = Resistor [tolerance=±5% resistance=330 package=THT]
  R5 = Resistor [tolerance=±5% resistance=100k package=THT]
  R6 = Resistor [tolerance=±5% resistance=100k package=THT]

nets:
  GND: NRF24L01+.GND, C1.-, Arduino1.GND, Q1.source, Power_plug1.GND, J2.pin2, Power_plug2.GND, LED1.common_cathode, R5.Pin_1, R6.Pin_1
  3.3V: NRF24L01+.VCC, C1.+
  CE: NRF24L01+.CE, Arduino1.D9
  CSN: NRF24L01+.CS, Arduino1.D10
  SCK: NRF24L01+.SCK, Arduino1.SCK
  MOSI: NRF24L01+.MOSI, Arduino1.MOSI
  MISO: NRF24L01+.MISO, Arduino1.MISO
  IRQ: NRF24L01+.IRQ, Arduino1.D2
  5V/BATTERY_STATUS: Arduino1.VCC, Arduino1.A6, Power_plug1.VCC, R6.Pin_0
  GREEN_LED: Arduino1.A4, R2.Pin_1
  RED_LED: Arduino1.A5, R3.Pin_1
  BLUE_LED: Arduino1.A3, R1.Pin_1
  COL3: Arduino1.A2, U1.3
  COL2: Arduino1.A1, U1.2
  COL1: Arduino1.A0, U1.1
  ROW1: Arduino1.D8, U1.4
  ROW2: Arduino1.D7, U1.5
  PIEZO: Arduino1.D6, J2.pin1
  SIREN: Arduino1.D5, R4.Pin_0
  ROW3: Arduino1.D4, U1.6
  ROW4: Arduino1.D3, U1.7
  N1: Q1.Gate, R4.Pin_1, R5.Pin_0
  N2: Q1.drain, J1.pin2
  12V: J1.pin1, Power_plug2.VCC
  N3: R1.Pin_0, LED1.blue_anode
  N4: LED1.red_anode, R3.Pin_0
  N5: LED1.green_anode, R2.Pin_0

notes:
  Siren, V1.0
