# Fritzing sketch Sound_Schema (saved by Fritzing 0.9.3b)
perfboards: 1

parts:
  NRF24L01+ = NRF24L01+ Breakout Board
  C1 = Electrolytic Capacitor [capacitance=4.7µF package="100 mil [THT, electrolytic]"]
  R1 = Resistor [tolerance=±5% resistance=220 package=THT]
  LED1 = RGB LED (com. cathode, rgb) [package="5 mm [THT]"]
  R2 = Resistor [tolerance=±5% resistance=220 package=THT]
  R3 = Resistor [tolerance=±5% resistance=220 package=THT]
  J5 = female pin header, 2 pins [form="♀ (female)" part_number="3.3V IN"]
  DFPlayer_Mini1 = DFPlayer MINI [package="DIP (Dual Inline) [THT]"]
  R7 = Resistor [tolerance=±5% resistance=1k package=THT]
  R8 = Resistor [tolerance=±5% resistance=1k package=THT]
  U1 = RELAY [package=relay-jzc]
  D1 = Rectifier Diode [part_number=1N4007 package="300 mil [THT]"]
  MOSFET1 = Basic FET N-Channel [part_number=2N7000 package="DPak [SMD]"]
  R9 = Resistor [tolerance=±5% resistance=100k package=THT]
  J6 = Screw terminal - 2 pins [part_number="220V IN" package=THT]
  J7 = Screw terminal - 2 pins [part_number="220V OUT" package=THT]
  Arduino1 = Arduino Pro Mini (3.3V)
  J8 = female pin header, 3 pins [form="♀ (female)" part_number=AUDIO]

nets:
  GND: NRF24L01+.GND, C1.-, LED1.common_cathode, J5.pin2, DFPlayer_Mini1.GND, MOSFET1.source, R9.Pin_0, Arduino1.GND, J8.pin3
  3.3V: NRF24L01+.VCC, C1.+, J5.pin1, DFPlayer_Mini1.VCC, U1.COIL1, D1.cathode, Arduino1.VCC
  CE: NRF24L01+.CE, Arduino1.D9
  CSN: NRF24L01+.CS, Arduino1.D10
  SCK: NRF24L01+.SCK, Arduino1.SCK
  MOSI: NRF24L01+.MOSI, Arduino1.MOSI
  MISO: NRF24L01+.MISO, Arduino1.MISO
  IRQ: NRF24L01+.IRQ, Arduino1.D2
  N1: R1.Pin_0, LED1.blue_anode
  BLUE_LED: R1.Pin_1, Arduino1.A3
  N2: LED1.red_anode, R3.Pin_0
  N3: LED1.green_anode, R2.Pin_0
  GREEN_LED: R2.Pin_1, Arduino1.A4
  RED_LED: R3.Pin_1, Arduino1.A5
  N4: DFPlayer_Mini1.RX, R7.Pin_1
  N5: DFPlayer_Mini1.TX, R8.Pin_1
  DAC_R: DFPlayer_Mini1.DAC_R, J8.pin1
  DAC_L: DFPlayer_Mini1.DAC_L, J8.pin2
  RX: R7.Pin_0, Arduino1.D7
  TX: R8.Pin_0, Arduino1.D8
  N6: U1.COIL2, D1.anode, MOSFET1.drain
  N7: U1.NO, J7.pin2
  N8: U1.MAIN, J6.pin1
  relay: MOSFET1.Gate, R9.Pin_1, Arduino1.D5
  N9: J6.pin2, J7.pin1

notes:
  Sound, V1.0

custom parts:
  DFPlayer MINI: MP3 module by DFRobot.com for playing Music from an SD-Card. Supports WAV and MP3 files.
