# Fritzing sketch sketch (saved by Fritzing 0.9.3b)
breadboards: 1

parts:
  Arduino_Pro_Mini_(3_3V) = Arduino Pro Mini (3.3V)
  MOSFET1 = MOSFET-NCHANNEL [part_number=2N7000 package=to-92]
  Relay_5V = RELAY [package=relay-t9a]
  Sector = AC Power [voltage=220V frequency=60]
  C1 = Ceramic Capacitor [capacitance=100nF package="100 mil [THT, multilayer]"]
  R1 = Resistor [tolerance=±5% resistance=100 package=THT]
  D1 = Rectifier Diode [part_number=1N4007 package="300 mil [THT]"]
  J1 = Screw terminal - 2 pins [package=THT]
  V5 = DC Power [voltage=5V]
  R2 = Resistor [tolerance=±5% resistance=10k package=THT]
  C2 = Electrolytic Capacitor [capacitance=100µF package="100 mil [THT, electrolytic]"]

nets:
  GND: Arduino_Pro_Mini_(3_3V).GND, MOSFET1.S, V5.V-, R2.Pin_0, C2.-
  5V: Arduino_Pro_Mini_(3_3V).RAW, Relay_5V.COIL1, D1.cathode, V5.V+, C2.+
  3.3V: Arduino_Pro_Mini_(3_3V).VCC
  N1: Arduino_Pro_Mini_(3_3V).D9, MOSFET1.G, R2.Pin_1
  N2: MOSFET1.D, Relay_5V.COIL2, D1.anode
  N3: Relay_5V.NO, C1.1, J1.pin2
  N4: Sector.V-, J1.pin1
  N5: C1.0, R1.Pin_1
